# Fritzing sketch data-producer-1-arduino (saved by Fritzing 0.9.3b)
breadboards: 1

parts:
  Part5 = Triple Axis Accelerometer Breakout - ADXL345
  LCM1602_IIC2 = LCM1602 IIC [part_number="LCM1602 IIC" chip_label="LCM1602 IIC" package="DIP (Dual Inline) [THT]"]
  LCD2 = LCD screen
  U1 = ESP8266 ESP-01 Upgraded WiFi Module [part_number=ESP8266]

nets:
  N1: Part5.SDA, Part5.SCL, LCM1602_IIC2.VCC, LCM1602_IIC2.SDA, LCM1602_IIC2.SCL, U1.RST/GPIO_16, U1.GPIO_2, U1.TXD
  VSS: LCM1602_IIC2.VSS, LCD2.VSS
  VDD: LCM1602_IIC2.VDD, LCD2.VDD
  N2: LCM1602_IIC2.V0, LCD2.V0
  N3: LCM1602_IIC2.RS, LCD2.RS
  N4: LCM1602_IIC2.RW, LCD2.R/W
  N5: LCM1602_IIC2.E, LCD2.E
  N6: LCM1602_IIC2.D0, LCD2.DB0
  N7: LCM1602_IIC2.D1, LCD2.DB1
  N8: LCM1602_IIC2.D2, LCD2.DB2
  N9: LCM1602_IIC2.D3, LCD2.DB3
  N10: LCM1602_IIC2.D4, LCD2.DB4
  N11: LCM1602_IIC2.D5, LCD2.DB5
  N12: LCM1602_IIC2.D6, LCD2.DB6
  N13: LCM1602_IIC2.D7, LCD2.DB7
  N14: LCM1602_IIC2.A, LCD2.LED+
  N15: LCM1602_IIC2.K, LCD2.LED-
  N16: LCM1602_IIC2.GND, U1.RXD
  N17: LCM1602_IIC2.LED_A, LCM1602_IIC2.LED_B

custom parts:
  LCM1602 IIC: I2C-Module to use a 1602 or 2004 LCD on with the wire.h libory Serial LCD Modul
  ESP8266 ESP-01 Upgraded WiFi Module: Upgraded Version ESP-01,all Flash are upgraded to 1M byte.Also support Cloud service remote transmission.
