# Fritzing sketch data-producer-2-arduino (saved by Fritzing 0.9.3b)
breadboards: 1

parts:
  GLCD_128x1 = 128 x 64 Graphic LCD  # not connected
  DHT1 = DHT11 Humitidy and Temperature Sensor
  FLO-30_Circuit1 = FLO-30 Circuit
  U2 = ESP8266 ESP-01 Upgraded WiFi Module [part_number=ESP8266]

nets:
  VDD: DHT1.VDD, FLO-30_Circuit1.Vcc
  N1: DHT1.DATA, U2.GPIO_2
  GND: DHT1.GND, FLO-30_Circuit1.GND
  N2: FLO-30_Circuit1.TX, U2.RXD
  N3: FLO-30_Circuit1.RX, U2.TXD
  N4: U2.VCC, U2.CH_PD

custom parts:
  DHT11 Humitidy and Temperature Sensor: DHT11 Humidity and Temperature Sensor
  ESP8266 ESP-01 Upgraded WiFi Module: Upgraded Version ESP-01,all Flash are upgraded to 1M byte.Also support Cloud service remote transmission.
