# Fritzing sketch data-producer-1-arduino (saved by Fritzing 0.9.3b)
breadboards: 1

parts:
  Part1 = Arduino Uno (Rev3)
  Part5 = Triple Axis Accelerometer Breakout - ADXL345
  LCM1602_IIC2 = LCM1602 IIC [part_number="LCM1602 IIC" chip_label="LCM1602 IIC" package="DIP (Dual Inline) [THT]"]
  LCD2 = LCD screen

nets:
  5V: Part1.A4/SDA, Part1.A5/SCL, Part1.5V, Part5.SDA, Part5.SCL, LCM1602_IIC2.VCC, LCM1602_IIC2.SDA, LCM1602_IIC2.SCL
  GND: Part1.GND, LCM1602_IIC2.GND
  VSS: LCM1602_IIC2.VSS, LCD2.VSS
  VDD: LCM1602_IIC2.VDD, LCD2.VDD
  N1: LCM1602_IIC2.V0, LCD2.V0
  N2: LCM1602_IIC2.RS, LCD2.RS
  N3: LCM1602_IIC2.RW, LCD2.R/W
  N4: LCM1602_IIC2.E, LCD2.E
  N5: LCM1602_IIC2.D0, LCD2.DB0
  N6: LCM1602_IIC2.D1, LCD2.DB1
  N7: LCM1602_IIC2.D2, LCD2.DB2
  N8: LCM1602_IIC2.D3, LCD2.DB3
  N9: LCM1602_IIC2.D4, LCD2.DB4
  N10: LCM1602_IIC2.D5, LCD2.DB5
  N11: LCM1602_IIC2.D6, LCD2.DB6
  N12: LCM1602_IIC2.D7, LCD2.DB7
  N13: LCM1602_IIC2.A, LCD2.LED+
  N14: LCM1602_IIC2.K, LCD2.LED-
  N15: LCM1602_IIC2.LED_A, LCM1602_IIC2.LED_B

custom parts:
  LCM1602 IIC: I2C-Module to use a 1602 or 2004 LCD on with the wire.h libory Serial LCD Modul
