# Fritzing sketch data-producer-1-esp-01 (saved by Fritzing 0.9.6b)
breadboards: 1

parts:
  GLCD_128x1 = 128 x 64 Graphic LCD  # not connected
  DHT1 = DHT11 Humitidy and Temperature Sensor
  FLO-30_Circuit1 = FLO-30 Circuit
  Espessif_Serial_Wifi_Modul_1 = ESP8266 ESP01 [part_number=ESP8266 package=THT]

nets:
  VCC: DHT1.VDD, FLO-30_Circuit1.Vcc, Espessif_Serial_Wifi_Modul_1.VCC, Espessif_Serial_Wifi_Modul_1.CH_PD
  N1: DHT1.DATA, Espessif_Serial_Wifi_Modul_1.GPIO02
  GND: DHT1.GND, FLO-30_Circuit1.GND, Espessif_Serial_Wifi_Modul_1.GND
  N2: FLO-30_Circuit1.TX, Espessif_Serial_Wifi_Modul_1.RXD
  N3: FLO-30_Circuit1.RX, Espessif_Serial_Wifi_Modul_1.TXD

notes:
  RX - TX connection to Screen

custom parts:
  DHT11 Humitidy and Temperature Sensor: DHT11 Humidity and Temperature Sensor
  ESP8266 ESP01: Generic WiFi Module based on the ESP8266 with onboard PCB antenna and UART communications
