# Fritzing sketch mqtt-and-mcp (saved by Fritzing 0.9.6b)
breadboards: 1

parts:
  U1 = ESP8266 NodeMCU LoLin base
  U2 = MCP23017 [package=dil28-3]
  LED1 = smd LED [color="Red (633nm)" package="0603 [SMD]"]
  LED2 = smd LED [color="Red (633nm)" package="0603 [SMD]"]
  LED3 = smd LED [color="Red (633nm)" package="0603 [SMD]"]
  LED4 = smd LED [color="Red (633nm)" package="0603 [SMD]"]
  R1 = Resistor [tolerance=±5% resistance=220 package="1206 [SMD]"]
  R2 = Resistor [tolerance=±5% resistance=220 package="1206 [SMD]"]

nets:
  N1: U1.GND1-0, U1.GND3-0, U1.GND3-2, U2.GND, U2.A0, U2.A1, U2.A2, LED1.cathode, LED2.cathode, LED3.cathode, LED4.cathode
  N2: U1.3V1-0, U1.3V1-1, U1.3V4, U2.VCC, U2.RESET, R1.Pin_0, R2.Pin_1
  N3: U1.D1-0, U1.D1-2, U1.D1-3, U2.SCL, R1.Pin_1
  N4: U1.D2-0, U1.D2-2, U2.SDA, R2.Pin_0
  N5: U2.GPB0, LED1.anode
  N6: U2.GPB1, LED2.anode
  N7: U2.GPB2, LED3.anode
  N8: U2.GPB3, LED4.anode

custom parts:
  ESP8266 NodeMCU LoLin base: ESP8266 based NodeMCU Base
  MCP23017: 16 bit I/O chip controlled via I2C
